# Fritzing sketch dash (saved by Fritzing 0.9.1b)
breadboards: 1

parts:
  Teensy_3_1 = Teensy 3.1
  ADXL1 = ADXL335 Accelerometer Breakout
  TFT1 = 1.8" TFT Display with uSD
  ENCODER1 = Rotary Encoder with Knob
  neopixel1 = Neopixel Ring 16
  C1 = Electrolytic Capacitor [capacitance=1mF voltage=6.3V package="100 mil [THT, electrolytic]"]
  IC1 = IC, DIP package, 8 pins [chip_label=IC]  # not connected

nets:
  GND: Teensy_3_1.GND, Teensy_3_1.AGND, ADXL1.GND, TFT1.BL, ENCODER1.no_name_yet#2, ENCODER1.no_name_yet#4, neopixel1.GND, C1.-
  N1: Teensy_3_1.D6, TFT1.GND
  N2: Teensy_3_1.D7, ENCODER1.no_name_yet#3
  N3: Teensy_3_1.D8, ENCODER1.no_name_yet#1
  N4: Teensy_3_1.A0/D14, ADXL1.Yout
  N5: Teensy_3_1.A1/D15, ADXL1.Zout
  VIN: Teensy_3_1.Vin, ADXL1.Vin, TFT1.MISO, neopixel1.VCC, C1.+

notes:
  SPST button connected to GND and D2, uses internal pull-up in the micro.

custom parts:
  ADXL335 Accelerometer Breakout: ADXL335 Accelerometer Breakout board
  1.8" TFT Display with uSD: 1.8" TFT Display with SPI control and MicroSD card
  Rotary Encoder with Knob: Rotary Encoder with 1/4" Shaft and Knob
  Neopixel Ring 16: Neopixel Ring x16

// code stored in the sketch: dash.ino
/*

Circuit / code information and documentation.
=============================


Display
------

The display used is ST7735 controlled 1.8" TFT. It use SPI to communicate with the uC.
The Teensy has hardware SPI which makes the communication with the display much faster than on the AVR.

*	A display tutorial including code for AVR can be found here: https://learn.adafruit.com/1-8-tft-display/
*	SPI optimization techniques can be found here: http://dorkbotpdx.org/blog/paul/display_spi_optimization;
	please note, this is for a different chipset but the same rules apply.
*	The modified Adafruit library which leverages the above techniques can be found here:
	https://github.com/PaulStoffregen/Adafruit_ST7735 and a small thread discussing this can be found here:
	https://forum.pjrc.com/threads/25045-Teensy-3-1-adafruit-1-8-18-bit-color-tft-SPI-speed
*	The base Adafruit library to draw graphics is also needed and can be found here:
	https://github.com/adafruit/Adafruit-GFX-Library


NEOPixels
--------

For shift-light and alarm indication a NEOPixel strip is used. Good documentation can be found on the
Adafruit website here: https://learn.adafruit.com/adafruit-neopixel-uberguide.

One thing to note is that the pixels need to be driven logically at supply voltage. So when using a 3.3v
uC a level shifter is needed. Comparison of level shifters can be found here: http://happyinmotion.com/?p=1247


Rotary encoder
------------

A rotary encoder tutorial can be found here: https://learn.adafruit.com/trinket-usb-volume-knob


Custom dial faces
---------------

In the end it may be required to make custom dial faces for the modifications done to the dash.
A very exhaustive tutorial can be found here: http://mazda626.net/topic/39309-making-custom-gauge-faces/


Inspiration
---------

*	Digital speedometer with Arduino and 7-segment display: http://matthewcmcmillan.blogspot.nl/2014/02/arduino-digital-speedometer.html
*	MPGuino and derivatives: http://ecomodder.com/wiki/index.php/MPGuino and http://mpguino.wiseman.ee/eng


*/
