# Fritzing sketch dash (saved by Fritzing 0.9.1b)
breadboards: 1

parts:
  Teensy_3_1 = Teensy 3.1
  Accelerometer = ADXL335 Accelerometer Breakout
  Display = 1.8" TFT Display with uSD
  Rotary/Pushbutton = Rotary Encoder with Knob
  U1 = Optocoupler [package=THT]
  R1 = Resistor [tolerance=±5% resistance=10k package=THT]
  R2 = Resistor [tolerance=±5% resistance=4.7k package=THT]
  D1 = Zener Diode [part_number=BZX85C breakdown_voltage=12.1V package="300 mil [THT]"]
  Shift/Warning_Light = Neopixel Strip -- Black (60/m)

nets:
  GND: Teensy_3_1.GND, Display.BL, Rotary/Pushbutton.no_name_yet#3, Rotary/Pushbutton.no_name_yet#5, U1.Pin_2, U1.Pin_4, D1.anode, Shift/Warning_Light.GND
  N1: Teensy_3_1.D2, Shift/Warning_Light.DI
  Park Distance: Teensy_3_1.D5
  N2: Teensy_3_1.D6, Display.GND
  N3: Teensy_3_1.D7, Rotary/Pushbutton.no_name_yet#4
  N4: Teensy_3_1.D8, Rotary/Pushbutton.no_name_yet#1
  N5: Teensy_3_1.D9, Display.MOSI
  N6: Teensy_3_1.D10, Display.SDCS
  N7: Teensy_3_1.D11, Display.D/C
  N8: Teensy_3_1.D12, Rotary/Pushbutton.no_name_yet#2
  N9: Teensy_3_1.D13, Display.RST
  N10: Teensy_3_1.A0/D14, Accelerometer.Zout
  N11: Teensy_3_1.A1/D15, Accelerometer.Yout
  N12: Teensy_3_1.A2/D16, Accelerometer.Xout
  N13: Teensy_3_1.A9/D23, R1.Pin_1
  5V: Teensy_3_1.Vin, Display.MISO, Shift/Warning_Light.+5V
  N14: U1.Pin_1, R2.Pin_0, D1.cathode
  N15: U1.Pin_5, R1.Pin_0

notes:
  SPST button connected to GND, uses internal pull-up in the micro.
  Serial (RX1 [0], TX1 [1]) and CAN (TX [3], RX [4]) are purposely left open for future enhancements.
  Teensy Dash, 0.2

custom parts:
  ADXL335 Accelerometer Breakout: ADXL335 Accelerometer Breakout board
  1.8" TFT Display with uSD: 1.8" TFT Display with SPI control and MicroSD card
  Rotary Encoder with Knob: Rotary Encoder with 1/4" Shaft and Knob
  Neopixel Strip -- Black (60/m): Neopixel Strip, Black, 60 pixels per meter.

// code stored in the sketch: dash.ino
/*

Circuit / code information and documentation.
=============================


Display
------

The display used is ST7735 controlled 1.8" TFT. It use SPI to communicate with the uC.
The Teensy has hardware SPI which makes the communication with the display much faster than on the AVR.

*	A display tutorial including code for AVR can be found here: https://learn.adafruit.com/1-8-tft-display/
*	SPI optimization techniques can be found here: http://dorkbotpdx.org/blog/paul/display_spi_optimization;
	please note, this is for a different chipset but the same rules apply.
*	The modified Adafruit library which leverages the above techniques can be found here:
	https://github.com/PaulStoffregen/Adafruit_ST7735 and a small thread discussing this can be found here:
	https://forum.pjrc.com/threads/25045-Teensy-3-1-adafruit-1-8-18-bit-color-tft-SPI-speed
*	The base Adafruit library to draw graphics is also needed and can be found here:
	https://github.com/adafruit/Adafruit-GFX-Library


NEOPixels
--------

For shift-light and alarm indication a NEOPixel strip is used. Good documentation can be found on the
Adafruit website here: https://learn.adafruit.com/adafruit-neopixel-uberguide.

One thing to note is that the pixels need to be driven logically at supply voltage. So when using a 3.3v
uC a level shifter is needed. Comparison of level shifters can be found here: http://happyinmotion.com/?p=1247


Rotary encoder
------------

A rotary encoder tutorial can be found here: https://learn.adafruit.com/trinket-usb-volume-knob


Custom dial faces
---------------

In the end it may be required to make custom dial faces for the modifications done to the dash.
A very exhaustive tutorial can be found here: http://mazda626.net/topic/39309-making-custom-gauge-faces/


Inspiration
---------

*	Digital speedometer with Arduino and 7-segment display: http://matthewcmcmillan.blogspot.nl/2014/02/arduino-digital-speedometer.html
*	MPGuino and derivatives: http://ecomodder.com/wiki/index.php/MPGuino and http://mpguino.wiseman.ee/eng


*/
